// Logisim project RBT_8_Bit_Processor.circ as structural Verilog
module Full_Adder_1bit (
  input  A,
  input  B,
  input  Cin,
  output Sum,
  output Cout
);

  wire and_1_out, and_2_out, xor_1_out;

  xor xor_1 (xor_1_out, A, B);
  and and_1 (and_1_out, A, B);
  xor xor_2 (Sum, xor_1_out, Cin);
  and and_2 (and_2_out, xor_1_out, Cin);
  or or_1 (Cout, and_1_out, and_2_out);
endmodule

module Adder_8bit (
  input  [7:0] A,
  input  [7:0] B,
  input  Cin,
  output [7:0] Sum,
  output Cout
);

  wire C1, C2, C3, C4, C5, C6, C7;

  Full_Adder_1bit FA0 (.A(A[0]), .B(B[0]), .Cin(Cin), .Sum(Sum[0]), .Cout(C1));
  Full_Adder_1bit FA1 (.A(A[1]), .B(B[1]), .Cin(C1), .Sum(Sum[1]), .Cout(C2));
  Full_Adder_1bit FA2 (.A(A[2]), .B(B[2]), .Cin(C2), .Sum(Sum[2]), .Cout(C3));
  Full_Adder_1bit FA3 (.A(A[3]), .B(B[3]), .Cin(C3), .Sum(Sum[3]), .Cout(C4));
  Full_Adder_1bit FA4 (.A(A[4]), .B(B[4]), .Cin(C4), .Sum(Sum[4]), .Cout(C5));
  Full_Adder_1bit FA5 (.A(A[5]), .B(B[5]), .Cin(C5), .Sum(Sum[5]), .Cout(C6));
  Full_Adder_1bit FA6 (.A(A[6]), .B(B[6]), .Cin(C6), .Sum(Sum[6]), .Cout(C7));
  Full_Adder_1bit FA7 (.A(A[7]), .B(B[7]), .Cin(C7), .Sum(Sum[7]), .Cout(Cout));

  // Other names for the same wires on the sheet: C0 = Cin; C8 = Cout; S0 = Sum[0]; S1 = Sum[1]; S2 = Sum[2];
  //   S3 = Sum[3]; S4 = Sum[4]; S5 = Sum[5]; S6 = Sum[6]; S7 = Sum[7]
endmodule

module AddSub_8bit (
  input  [7:0] A,
  input  SUB,
  input  [7:0] B,
  output [7:0] Result,
  output Cout,
  output Zero
);

  wire [7:0] bit_extender_1_out, xor_1_out;

  assign bit_extender_1_out = {{7{SUB}}, SUB};  // Bit_Extender bit_extender_1
  assign xor_1_out = bit_extender_1_out ^ B;  // XOR_Gate xor_1, 8 bits wide
  Comparator #(.mode("unsigned")) comparator_1 (.a(Result), .b({8{1'b0}}), .eq(Zero));  // open: gt, lt
  Adder_8bit adder_8bit_1 (.A(A), .B(xor_1_out), .Cin(SUB), .Sum(Result), .Cout(Cout));
endmodule

module ALU_8bit (
  input  [7:0] A,
  input  [7:0] B,
  input  [1:0] OP,
  output Carry,
  output Zero,
  output [7:0] Result
);

  wire [7:0] addsub_8bit_1_result, and_1_out, or_1_out;

  assign and_1_out = A & B;  // AND_Gate and_1, 8 bits wide
  assign or_1_out = A | B;  // OR_Gate or_1, 8 bits wide
  AddSub_8bit addsub_8bit_1 (.A(A), .SUB(OP[0]), .B(B), .Result(addsub_8bit_1_result), .Cout(Carry));  // open: Zero
  Multiplexer #(.select(2), .width(8)) multiplexer_1 (
    .in0(addsub_8bit_1_result), .in1(addsub_8bit_1_result), .in2(and_1_out), .in3(or_1_out), .out(Result),
    .sel(OP));
  Comparator #(.mode("unsigned")) comparator_1 (.a(Result), .b({8{1'b0}}), .eq(Zero));  // open: gt, lt
endmodule

module Register_8bit (
  input  [7:0] DataIn,
  input  Load,
  input  Clock,
  input  Reset,
  output [7:0] DataOut
);

  Register register_1 (.D(DataIn), .en(Load), .clk(Clock), .Q(DataOut), .clr(Reset));
endmodule

module Program_Counter_4bit (
  input  Reset,
  input  Load,
  input  Enable,
  input  Clock,
  input  [3:0] AddressIn,
  output [3:0] AddressOut
);

  Counter #(.max('hf), .width(4)) counter_1 (
    .clr(Reset), .load(Load), .up(1'b1), .count(Enable), .clk(Clock), .D(AddressIn), .Q(AddressOut));  // open: carry
endmodule

module Instruction_Memory_16x8 (
  input  [3:0] Address,
  output [7:0] Instruction
);

  ROM #(.addrWidth(4)) rom_1 (.addr(Address), .data(Instruction));

  // Notes on the sheet:
  //   contents of rom_1 (hex, n*v repeats v):
  //   15 3e 13 4e 80 f0
endmodule

module Instruction_Decoder (
  input  [7:0] Instruction,
  output [3:0] Operand,
  output [3:0] Opcode
);


  assign Opcode = Instruction[7:4];
  assign Operand = Instruction[3:0];
endmodule

module Control_Unit (
  input  [3:0] Opcode,
  input  Zero,
  output PCEnable,
  output OutLoad,
  output Halt,
  output AccLoad,
  output MemWrite,
  output PCLoad,
  output [1:0] AccSel,
  output [1:0] ALUOp
);

  wire ADD, and_1_out, JMP, JZ, LDI;

  Decoder #(.enable("false"), .select(4)) decoder_1 (
    .out1(LDI), .out2(AccSel[0]), .out3(MemWrite), .out4(ADD), .out5(ALUOp[0]), .out6(JMP), .out7(JZ),
    .out8(OutLoad), .out15(Halt), .sel(Opcode));  // open: out0, out9, out10, out11, out12, out13, out14
  and and_1 (and_1_out, JZ, Zero);
  or or_1 (AccSel[1], ADD, ALUOp[0]);
  not not_1 (PCEnable, Halt);
  or or_2 (AccLoad, LDI, AccSel[0], ADD, ALUOp[0]);
  or or_3 (PCLoad, JMP, and_1_out);

  assign ALUOp[1] = 1'b0;

  // Other names for the same wires on the sheet: LDA = AccSel[0]; SUB = ALUOp[0]; HLT = Halt; OPT = OutLoad;
  //   STA = MemWrite
endmodule

module Data_Memory_16x8 (
  input  [3:0] Address,
  input  WriteEnable,
  input  Clock,
  input  [7:0] DataIn,
  output [7:0] DataOut
);

  RAM #(.addrWidth(4), .enables("line")) ram_1 (
    .addr(Address), .we(WriteEnable), .clk(Clock), .din(DataIn), .dout(DataOut));
endmodule

module CPU_8bit (
  input  Reset,
  input  Clock,
  output Halted,
  output ZeroFlag,
  output [7:0] DisplayOut,
  output [3:0] PCValue,
  output [7:0] IRValue,
  output [7:0] AccValue
);

  wire ACC_LOAD, MEM_WRITE, OUT_LOAD, PC_ENABLE, PC_LOAD, undriven;
  wire [1:0] ACC_SEL, ALU_OP;
  wire [3:0] instruction_decoder_1_opcode, OPERAND_BUS;
  wire [7:0] ACC_IN, ALU_RESULT, bit_extender_1_out, MEM_BUS;

  Comparator #(.mode("unsigned")) comparator_1 (.a(AccValue), .b({8{1'b0}}), .eq(ZeroFlag));  // open: gt, lt
  assign bit_extender_1_out = {{4{1'b0}}, OPERAND_BUS};  // Bit_Extender bit_extender_1
  Multiplexer #(.select(2), .width(8)) multiplexer_1 (
    .in0(bit_extender_1_out), .in1(MEM_BUS), .in2(ALU_RESULT), .in3({8{1'b0}}), .out(ACC_IN), .sel(ACC_SEL));
  Program_Counter_4bit program_counter_4bit_1 (
    .Reset(Reset), .Load(undriven), .Enable(PC_ENABLE), .Clock(Clock), .AddressIn(OPERAND_BUS),
    .AddressOut(PCValue));
  Data_Memory_16x8 data_memory_16x8_1 (
    .Address(OPERAND_BUS), .WriteEnable(MEM_WRITE), .Clock(Clock), .DataIn(AccValue), .DataOut(MEM_BUS));
  Register_8bit OUT_REG (.DataIn(AccValue), .Load(OUT_LOAD), .Clock(Clock), .Reset(Reset), .DataOut(DisplayOut));
  Instruction_Memory_16x8 instruction_memory_16x8_1 (.Address(PCValue), .Instruction(IRValue));
  Register_8bit ACC (.DataIn(ACC_IN), .Load(ACC_LOAD), .Clock(Clock), .Reset(Reset), .DataOut(AccValue));
  Control_Unit control_unit_1 (
    .Opcode(instruction_decoder_1_opcode), .Zero(ZeroFlag), .PCEnable(PC_ENABLE), .OutLoad(OUT_LOAD),
    .Halt(Halted), .AccLoad(ACC_LOAD), .MemWrite(MEM_WRITE), .PCLoad(PC_LOAD), .AccSel(ACC_SEL),
    .ALUOp(ALU_OP));
  Instruction_Decoder instruction_decoder_1 (
    .Instruction(IRValue), .Operand(OPERAND_BUS), .Opcode(instruction_decoder_1_opcode));
  ALU_8bit alu_8bit_1 (.A(AccValue), .B(MEM_BUS), .OP(ALU_OP), .Result(ALU_RESULT));  // open: Carry, Zero

  // Other names for the same wires on the sheet: ACC_BUS[7:0] = AccValue; CLK = Clock; DISPLAY_BUS[7:0] = DisplayOut;
  //   HALT_SIG = Halted; RST = Reset; ZERO_SIG = ZeroFlag
endmodule
